// Digital circuit Decodificador.dig as structural Verilog
module Decodificador (
  input  E1,
  input  E2,
  input  E3,
  input  E4,
  output LDA,
  output ADD,
  output SUB,
  output OUT,
  output HLT
);

  wire not_1_out, not_2_out, not_3_out, not_4_out;

  not not_1 (not_1_out, E4);
  not not_2 (not_2_out, E3);
  not not_3 (not_3_out, E2);
  not not_4 (not_4_out, E1);
  and and_1 (LDA, not_1_out, not_2_out, not_3_out, not_4_out);
  and and_2 (ADD, not_1_out, not_2_out, not_3_out, E1);
  and and_3 (SUB, not_1_out, not_2_out, E2, not_4_out);
  and and_4 (OUT, not_1_out, not_2_out, E2, E1);
  and and_5 (HLT, not_1_out, E3, not_3_out, not_4_out);
endmodule
